# Fritzing sketch cheap_radiowecker (saved by Fritzing 0.9.3b)

parts:
  U1 = ESP32 DevKitc V4 [part_number="ESP32_DEVKIT C V4"]
  IS2_2 = Adafruit MAX98357A I2S 3W Class D Amplifier [part_number=MAX98357A]
  Speaker = Piezo Speaker
  IS2_1 = Adafruit MAX98357A I2S 3W Class D Amplifier [part_number=MAX98357A]
  Speaker_2 = Piezo Speaker
  R2 = Resistor [tolerance=±5% resistance=470k package=THT]
  TFT = TFT 3.5 inch 480x320 w touch and SD [part_number=TFT_LCD_2.8_TOUCH]
  Q1 = pnp-Powertransistor [part_number=BC807-40 package="TO220 [THT]"]
  R1 = Resistor [tolerance=±5% resistance=1k package=THT]

nets:
  N1: U1.IO15, R1.Pin_0
  N2: U1.IO4, TFT.D/C
  N3: U1.IO5, TFT.CS
  N4: U1.IO18, TFT.SCK, TFT.T_CLK
  N5: U1.IO19, TFT.MISO, TFT.T_DO
  N6: U1.IO22, TFT.RST
  N7: U1.IO23, TFT.MOSI, TFT.T_DIN
  GND: U1.GND, IS2_2.GND, IS2_2.GAIN, IS2_1.GND, IS2_1.GAIN, TFT.GND
  3V3: U1.3V3, TFT.VCC, Q1.emitter
  N8: U1.IO33, IS2_2.DIN, IS2_1.DIN
  N9: U1.IO25, IS2_2.LRCLK, IS2_1.LRCLK
  N10: U1.IO26, IS2_2.BCLK, IS2_1.BCLK
  N11: U1.IO27, TFT.T_IRQ
  N12: U1.IO14, TFT.T_CS
  VIN: U1.5V, IS2_2.VIN, IS2_2.SD_MODE, IS2_1.VIN, R2.Pin_0
  N13: IS2_2.VO-, Speaker.pin1
  N14: IS2_2.VO+, Speaker.pin2
  N15: IS2_1.SD_MODE, R2.Pin_1
  N16: IS2_1.VO-, Speaker_2.pin1
  N17: IS2_1.VO+, Speaker_2.pin2
  N18: TFT.LED, Q1.collector
  N19: Q1.base, R1.Pin_1

custom parts:
  ESP32 DevKitc V4: ESP32-DevKitC board with ESP32-WROOM-32 module. ESP32-DevKitC V4 is a small-sized ESP32-based development board produced by Espressif. Most of the pins on the ESP module are broken out to the pin headers on the board. The pins D0, D1, D2, D3, CMD and CLK are used internally for communication between ESP32 and SPI flash memory. They are grouped on both sides near the USB connector. Avoid using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
  Adafruit MAX98357A I2S 3W Class D Amplifier: Listen to this good news - we now have an all in one digital audio amp breakout board that works incredibly well with the Raspberry Pi! If you're looking for an easy and low cost way to get you digital sound files bumpin' then the MAX08357 I2S Amp Breakout is for you. It takes standard I2S digital audio input and, not only decodes it into analog, but also amplifies it directly into a speaker.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
  TFT 3.5 inch 480x320 w touch and SD: This is a generic 1.8 tft spi lcd display available on ebay and others. The 1.8"3.5 inch 480X320 SPI TFT Module 320x480 LCD Display - Touch.
