# Fritzing sketch min_radiowecker (saved by Fritzing 0.9.3b)

parts:
  U1 = ESP32 DevKitc V4 [part_number="ESP32_DEVKIT C V4"]
  IS2_2 = Adafruit MAX98357A I2S 3W Class D Amplifier [part_number=MAX98357A]
  Speaker = Piezo Speaker
  IS2_1 = Adafruit MAX98357A I2S 3W Class D Amplifier [part_number=MAX98357A]
  Speaker_2 = Piezo Speaker
  R2 = Resistor [tolerance=±5% resistance=470k package=THT]

nets:
  GND: U1.GND, IS2_2.GND, IS2_2.GAIN, IS2_1.GND, IS2_1.GAIN
  N1: U1.IO33, IS2_2.DIN, IS2_1.DIN
  N2: U1.IO25, IS2_2.LRCLK, IS2_1.LRCLK
  N3: U1.IO26, IS2_2.BCLK, IS2_1.BCLK
  VIN: U1.5V, IS2_2.VIN, IS2_2.SD_MODE, IS2_1.VIN, R2.Pin_0
  N4: IS2_2.VO-, Speaker.pin1
  N5: IS2_2.VO+, Speaker.pin2
  N6: IS2_1.SD_MODE, R2.Pin_1
  N7: IS2_1.VO-, Speaker_2.pin1
  N8: IS2_1.VO+, Speaker_2.pin2

custom parts:
  ESP32 DevKitc V4: ESP32-DevKitC board with ESP32-WROOM-32 module. ESP32-DevKitC V4 is a small-sized ESP32-based development board produced by Espressif. Most of the pins on the ESP module are broken out to the pin headers on the board. The pins D0, D1, D2, D3, CMD and CLK are used internally for communication between ESP32 and SPI flash memory. They are grouped on both sides near the USB connector. Avoid using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
  Adafruit MAX98357A I2S 3W Class D Amplifier: Listen to this good news - we now have an all in one digital audio amp breakout board that works incredibly well with the Raspberry Pi! If you're looking for an easy and low cost way to get you digital sound files bumpin' then the MAX08357 I2S Amp Breakout is for you. It takes standard I2S digital audio input and, not only decodes it into analog, but also amplifies it directly into a speaker.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
